# Fritzing sketch pptls (saved by Fritzing 0.9.2b)
circuit board: 8.46667cm x 5.64444cm
breadboards: 1

parts:
  Parte1 = Arduino Uno (Rev3) - ICSP
  S2 = Momentary Switch [package=ksa_sealed_tac_switch]
  S3 = Momentary Switch [package=ksa_sealed_tac_switch]
  S4 = Momentary Switch [package=ksa_sealed_tac_switch]
  S6 = Momentary Switch [package=ksa_sealed_tac_switch]
  S7 = Momentary Switch [package=ksa_sealed_tac_switch]
  R1 = Resistor [tolerance=±5% resistance=220 package="2010 [SMD]"]
  R2 = Resistor [tolerance=±5% resistance=220 package="2010 [SMD]"]
  R3 = Resistor [tolerance=±5% resistance=220 package="2010 [SMD]"]
  R4 = Resistor [tolerance=±5% resistance=220 package="2010 [SMD]"]
  R5 = Resistor [tolerance=±5% resistance=220 package="2010 [SMD]"]

nets:
  N1: Parte1.5V, S2.3, S3.3, S4.3, S6.3, S7.3
  N2: Parte1.GND, R1.Pin_1, R2.Pin_1, R3.Pin_1, R4.Pin_1, R5.Pin_1
  N3: Parte1.D8, S7.1, R5.Pin_0
  N4: Parte1.D9_PWM, S6.1, R4.Pin_0
  N5: Parte1.D10_PWM/SS, S4.1, R3.Pin_0
  N6: Parte1.D11_PWM/MOSI, S3.1, R2.Pin_0
  N7: Parte1.D12/MISO, S2.1, R1.Pin_0
